// Digital circuit CPUDataPath.dig as structural Verilog
module CPUDataPath (
  output z,
  output n,
  output c,
  output o,
  output [3:0] ALU_Sel,
  output [1:0] MUX_Ctrl
);

  wire alu_1_p1, alu_1_p2, multiplexer_1_out;

  Seven_Seg_Hex seven_seg_hex_1 ();  // open: d, dp
  Multiplexer #(.Selector_Bits(2)) multiplexer_1 (
    .sel(MUX_Ctrl), .out(multiplexer_1_out));  // open: in_0, in_1, in_2, in_3
  // ALU alu_1: pin names not known; wires that end beside it: alu_1_p1, alu_1_p2, ALU_Sel[0], ALU_Sel[1], o, ALU_Sel[2], c, ALU_Sel[3], n, multiplexer_1_out, z, alu_1_p2, alu_1_p1
  Seven_Seg_Hex seven_seg_hex_2 ();  // open: d, dp
  // Pins of 1 and 2 bits meet at MUX_Ctrl
  // Pins of 1 and 4 bits meet at ALU_Sel
endmodule
